// Logisim project Rom.circ as structural Verilog: 1 circuit, main circuit main
module main (
  input  Seletor_de_bloco,
  input  in_2,
  input  Seletor_de_linha,
  input  in_4,
  input  in_5,
  input  in_6,
  input  in_7,
  input  in_8,
  input  in_9,
  input  in_10,
  input  in_11,
  input  in_12,
  input  in_13,
  input  in_14,
  input  in_15,
  input  in_16,
  input  in_17,
  input  in_18,
  input  in_19,
  input  in_20,
  input  in_21,
  input  in_22,
  input  in_23,
  input  in_24,
  input  in_25,
  input  in_26,
  input  in_27,
  input  in_28,
  input  in_29,
  input  in_30,
  input  in_31,
  input  in_32,
  input  in_33,
  input  in_34,
  input  in_35,
  input  in_36,
  input  in_37,
  input  in_38,
  input  in_39,
  input  in_40,
  input  in_41,
  input  in_42,
  input  in_43,
  input  in_44,
  input  in_45,
  input  in_46,
  input  in_47,
  input  in_48,
  input  in_49,
  input  in_50,
  input  in_51,
  input  in_52,
  input  in_53,
  input  in_54,
  input  in_55,
  input  in_56,
  input  in_57,
  input  in_58,
  input  in_59,
  input  in_60,
  input  in_61,
  input  in_62,
  input  in_63,
  input  in_64,
  input  in_65,
  input  in_66,
  input  in_67,
  input  in_68,
  output out_69,
  output Bits_armazenados,
  output out_71,
  output out_72
);

  wire and_1_out, and_2_out, and_3_out, and_4_out, and_5_out, and_6_out, and_7_out, and_8_out, and_9_out,
       and_10_out, and_11_out, and_12_out, and_13_out, and_14_out, and_15_out, and_16_out, and_17_out,
       and_18_out, and_19_out, and_20_out, and_21_out, and_22_out, and_23_out, and_24_out, and_25_out,
       and_26_out, and_27_out, and_28_out, and_29_out, and_30_out, and_31_out, and_32_out, and_33_out,
       and_34_out, and_35_out, and_36_out;

  and and_1 (and_1_out, ~in_2, ~Seletor_de_bloco);  // AND_Gate
  and and_2 (and_2_out, in_2, ~Seletor_de_bloco);  // AND_Gate
  and and_3 (and_3_out, ~in_2, Seletor_de_bloco);  // AND_Gate
  and and_4 (and_4_out, in_2, Seletor_de_bloco);
  and and_5 (and_5_out, ~in_4, ~Seletor_de_linha);  // AND_Gate
  and and_6 (and_6_out, in_4, ~Seletor_de_linha);  // AND_Gate
  and and_7 (and_7_out, ~in_4, Seletor_de_linha);  // AND_Gate
  and and_8 (and_8_out, in_4, Seletor_de_linha);
  and and_9 (and_9_out, ~in_4, ~Seletor_de_linha);  // AND_Gate
  and and_10 (and_10_out, in_4, ~Seletor_de_linha);  // AND_Gate
  and and_11 (and_11_out, ~in_4, Seletor_de_linha);  // AND_Gate
  and and_12 (and_12_out, in_4, Seletor_de_linha);
  and and_13 (and_13_out, ~in_4, ~Seletor_de_linha);  // AND_Gate
  and and_14 (and_14_out, in_4, ~Seletor_de_linha);  // AND_Gate
  and and_15 (and_15_out, ~in_4, Seletor_de_linha);  // AND_Gate
  and and_16 (and_16_out, in_4, Seletor_de_linha);
  and and_17 (and_17_out, ~in_4, ~Seletor_de_linha);  // AND_Gate
  and and_18 (and_18_out, in_4, ~Seletor_de_linha);  // AND_Gate
  and and_19 (and_19_out, ~in_4, Seletor_de_linha);  // AND_Gate
  and and_20 (and_20_out, in_4, Seletor_de_linha);
  and and_21 (and_21_out, and_5_out, and_1_out);
  assign out_69 = and_21_out ? in_5 : 1'bz;  // Controlled_Buffer controlled_buffer_1
  and and_22 (and_22_out, and_6_out, and_1_out);
  assign out_69 = and_22_out ? in_9 : 1'bz;  // Controlled_Buffer controlled_buffer_2
  and and_23 (and_23_out, and_7_out, and_1_out);
  assign out_69 = and_23_out ? in_13 : 1'bz;  // Controlled_Buffer controlled_buffer_3
  and and_24 (and_24_out, and_8_out, and_1_out);
  assign out_69 = and_24_out ? in_17 : 1'bz;  // Controlled_Buffer controlled_buffer_4
  and and_25 (and_25_out, and_9_out, and_2_out);
  assign out_69 = and_25_out ? in_21 : 1'bz;  // Controlled_Buffer controlled_buffer_5
  and and_26 (and_26_out, and_10_out, and_2_out);
  assign out_69 = and_26_out ? in_25 : 1'bz;  // Controlled_Buffer controlled_buffer_6
  and and_27 (and_27_out, and_11_out, and_2_out);
  assign out_69 = and_27_out ? in_29 : 1'bz;  // Controlled_Buffer controlled_buffer_7
  and and_28 (and_28_out, and_12_out, and_2_out);
  assign out_69 = and_28_out ? in_33 : 1'bz;  // Controlled_Buffer controlled_buffer_8
  and and_29 (and_29_out, and_13_out, and_3_out);
  assign out_69 = and_29_out ? in_37 : 1'bz;  // Controlled_Buffer controlled_buffer_9
  and and_30 (and_30_out, and_14_out, and_3_out);
  assign out_69 = and_30_out ? in_41 : 1'bz;  // Controlled_Buffer controlled_buffer_10
  and and_31 (and_31_out, and_15_out, and_3_out);
  assign out_69 = and_31_out ? in_45 : 1'bz;  // Controlled_Buffer controlled_buffer_11
  and and_32 (and_32_out, and_16_out, and_3_out);
  assign out_69 = and_32_out ? in_49 : 1'bz;  // Controlled_Buffer controlled_buffer_12
  and and_33 (and_33_out, and_17_out, and_4_out);
  assign out_69 = and_33_out ? in_53 : 1'bz;  // Controlled_Buffer controlled_buffer_13
  and and_34 (and_34_out, and_18_out, and_4_out);
  assign out_69 = and_34_out ? in_57 : 1'bz;  // Controlled_Buffer controlled_buffer_14
  and and_35 (and_35_out, and_19_out, and_4_out);
  assign out_69 = and_35_out ? in_61 : 1'bz;  // Controlled_Buffer controlled_buffer_15
  and and_36 (and_36_out, and_20_out, and_4_out);
  assign out_69 = and_36_out ? in_65 : 1'bz;  // Controlled_Buffer controlled_buffer_16
  assign Bits_armazenados = and_21_out ? in_6 : 1'bz;  // Controlled_Buffer controlled_buffer_17
  assign Bits_armazenados = and_22_out ? in_10 : 1'bz;  // Controlled_Buffer controlled_buffer_18
  assign Bits_armazenados = and_23_out ? in_14 : 1'bz;  // Controlled_Buffer controlled_buffer_19
  assign Bits_armazenados = and_24_out ? in_18 : 1'bz;  // Controlled_Buffer controlled_buffer_20
  assign Bits_armazenados = and_25_out ? in_22 : 1'bz;  // Controlled_Buffer controlled_buffer_21
  assign Bits_armazenados = and_26_out ? in_26 : 1'bz;  // Controlled_Buffer controlled_buffer_22
  assign Bits_armazenados = and_27_out ? in_30 : 1'bz;  // Controlled_Buffer controlled_buffer_23
  assign Bits_armazenados = and_28_out ? in_34 : 1'bz;  // Controlled_Buffer controlled_buffer_24
  assign Bits_armazenados = and_29_out ? in_38 : 1'bz;  // Controlled_Buffer controlled_buffer_25
  assign Bits_armazenados = and_30_out ? in_42 : 1'bz;  // Controlled_Buffer controlled_buffer_26
  assign Bits_armazenados = and_31_out ? in_46 : 1'bz;  // Controlled_Buffer controlled_buffer_27
  assign Bits_armazenados = and_32_out ? in_50 : 1'bz;  // Controlled_Buffer controlled_buffer_28
  assign Bits_armazenados = and_33_out ? in_54 : 1'bz;  // Controlled_Buffer controlled_buffer_29
  assign Bits_armazenados = and_34_out ? in_58 : 1'bz;  // Controlled_Buffer controlled_buffer_30
  assign Bits_armazenados = and_35_out ? in_62 : 1'bz;  // Controlled_Buffer controlled_buffer_31
  assign Bits_armazenados = and_36_out ? in_66 : 1'bz;  // Controlled_Buffer controlled_buffer_32
  assign out_71 = and_21_out ? in_7 : 1'bz;  // Controlled_Buffer controlled_buffer_33
  assign out_71 = and_22_out ? in_11 : 1'bz;  // Controlled_Buffer controlled_buffer_34
  assign out_71 = and_23_out ? in_15 : 1'bz;  // Controlled_Buffer controlled_buffer_35
  assign out_71 = and_24_out ? in_19 : 1'bz;  // Controlled_Buffer controlled_buffer_36
  assign out_71 = and_25_out ? in_23 : 1'bz;  // Controlled_Buffer controlled_buffer_37
  assign out_71 = and_26_out ? in_27 : 1'bz;  // Controlled_Buffer controlled_buffer_38
  assign out_71 = and_27_out ? in_31 : 1'bz;  // Controlled_Buffer controlled_buffer_39
  assign out_71 = and_28_out ? in_35 : 1'bz;  // Controlled_Buffer controlled_buffer_40
  assign out_71 = and_29_out ? in_39 : 1'bz;  // Controlled_Buffer controlled_buffer_41
  assign out_71 = and_30_out ? in_43 : 1'bz;  // Controlled_Buffer controlled_buffer_42
  assign out_71 = and_31_out ? in_47 : 1'bz;  // Controlled_Buffer controlled_buffer_43
  assign out_71 = and_32_out ? in_51 : 1'bz;  // Controlled_Buffer controlled_buffer_44
  assign out_71 = and_33_out ? in_55 : 1'bz;  // Controlled_Buffer controlled_buffer_45
  assign out_71 = and_34_out ? in_59 : 1'bz;  // Controlled_Buffer controlled_buffer_46
  assign out_71 = and_35_out ? in_63 : 1'bz;  // Controlled_Buffer controlled_buffer_47
  assign out_71 = and_36_out ? in_67 : 1'bz;  // Controlled_Buffer controlled_buffer_48
  assign out_72 = and_21_out ? in_8 : 1'bz;  // Controlled_Buffer controlled_buffer_49
  assign out_72 = and_22_out ? in_12 : 1'bz;  // Controlled_Buffer controlled_buffer_50
  assign out_72 = and_23_out ? in_16 : 1'bz;  // Controlled_Buffer controlled_buffer_51
  assign out_72 = and_24_out ? in_20 : 1'bz;  // Controlled_Buffer controlled_buffer_52
  assign out_72 = and_25_out ? in_24 : 1'bz;  // Controlled_Buffer controlled_buffer_53
  assign out_72 = and_26_out ? in_28 : 1'bz;  // Controlled_Buffer controlled_buffer_54
  assign out_72 = and_27_out ? in_32 : 1'bz;  // Controlled_Buffer controlled_buffer_55
  assign out_72 = and_28_out ? in_36 : 1'bz;  // Controlled_Buffer controlled_buffer_56
  assign out_72 = and_29_out ? in_40 : 1'bz;  // Controlled_Buffer controlled_buffer_57
  assign out_72 = and_30_out ? in_44 : 1'bz;  // Controlled_Buffer controlled_buffer_58
  assign out_72 = and_31_out ? in_48 : 1'bz;  // Controlled_Buffer controlled_buffer_59
  assign out_72 = and_32_out ? in_52 : 1'bz;  // Controlled_Buffer controlled_buffer_60
  assign out_72 = and_33_out ? in_56 : 1'bz;  // Controlled_Buffer controlled_buffer_61
  assign out_72 = and_34_out ? in_60 : 1'bz;  // Controlled_Buffer controlled_buffer_62
  assign out_72 = and_35_out ? in_64 : 1'bz;  // Controlled_Buffer controlled_buffer_63
  assign out_72 = and_36_out ? in_68 : 1'bz;  // Controlled_Buffer controlled_buffer_64

  // Notes on the sheet:
  //   Projeto 1- mória ROM
endmodule
