// Logisim project ULA.circ as structural Verilog: 1 circuit, main circuit main
module main (
  input  in_1,
  input  in_2,
  input  in_3,
  input  in_4,
  input  in_5,
  input  in_6,
  input  in_7,
  input  in_8,
  input  in_9,
  input  in_10,
  input  in_11,
  input  in_12,
  input  in_13,
  input  in_14,
  input  in_15,
  input  in_16,
  input  in_17,
  input  in_18,
  input  in_19,
  input  in_20,
  output out_21,
  output out_22,
  output out_23,
  output out_24
);

  wire and_1_out, and_2_out, and_3_out, and_4_out, and_5_out, and_6_out, and_7_out, and_8_out, and_9_out,
       and_10_out, and_11_out, and_12_out, and_13_out, and_14_out, and_15_out, and_16_out, and_17_out,
       and_18_out, and_19_out, and_20_out, and_21_out, and_22_out, and_23_out, and_24_out, and_25_out,
       or_1_out, or_2_out, or_3_out, or_4_out, or_5_out, or_6_out, or_7_out, or_8_out, or_9_out, or_10_out,
       or_11_out, or_12_out, or_13_out, or_14_out, undriven, undriven_2, undriven_3, undriven_4, undriven_5,
       undriven_6, undriven_7, xor_1_out, xor_2_out, xor_3_out, xor_4_out, xor_5_out, xor_6_out, xor_7_out,
       xor_8_out, xor_13_out, xor_14_out, xor_15_out, xor_16_out, xor_17_out, xor_18_out, xor_19_out,
       xor_20_out, xor_21_out, xor_23_out, xor_25_out, xor_27_out, xor_28_out, xor_29_out;

  xor xor_1 (xor_1_out, in_1, in_9);
  xor xor_2 (xor_2_out, in_2, in_9);
  xor xor_3 (xor_3_out, in_3, in_9);
  xor xor_4 (xor_4_out, in_4, in_9);
  xor xor_5 (xor_5_out, in_5, in_10);
  xor xor_6 (xor_6_out, in_6, in_10);
  xor xor_7 (xor_7_out, in_7, in_10);
  xor xor_8 (xor_8_out, in_8, in_10);
  // XOR_Gate xor_9 has open pins: in0=in_13, in1=undriven_2, out=open
  // XOR_Gate xor_10 has open pins: in0=in_14, in1=undriven, out=open
  // XOR_Gate xor_11 has open pins: in0=in_15, in1=undriven_2, out=open
  // XOR_Gate xor_12 has open pins: in0=in_16, in1=undriven, out=open
  xor xor_13 (xor_13_out, in_17, undriven_2);
  xor xor_14 (xor_14_out, in_18, undriven);
  xor xor_15 (xor_15_out, in_19, undriven_2);
  xor xor_16 (xor_16_out, in_20, undriven);
  and and_1 (and_1_out, xor_5_out, ~in_11);  // AND_Gate
  and and_2 (and_2_out, xor_6_out, ~in_11);  // AND_Gate
  and and_3 (and_3_out, xor_7_out, ~in_11);  // AND_Gate
  and and_4 (and_4_out, xor_8_out, ~in_11);  // AND_Gate
  xor xor_17 (xor_17_out, xor_13_out, undriven_3);
  xor xor_18 (xor_18_out, xor_17_out, xor_14_out);
  and and_5 (and_5_out, xor_13_out, undriven_3);
  or or_1 (or_1_out, and_5_out, and_6_out);
  and and_6 (and_6_out, xor_13_out, xor_14_out);
  and and_7 (and_7_out, undriven_3, xor_14_out);
  xor xor_19 (xor_19_out, xor_15_out, undriven_4);
  xor xor_20 (xor_20_out, xor_19_out, xor_16_out);
  and and_8 (and_8_out, xor_15_out, undriven_4);
  or or_2 (or_2_out, and_8_out, and_9_out);
  and and_9 (and_9_out, xor_15_out, xor_16_out);
  and and_10 (and_10_out, undriven_4, xor_16_out);
  or or_3 (or_3_out, or_1_out, and_7_out);
  or or_4 (or_4_out, or_2_out, and_10_out);
  xor xor_21 (xor_21_out, xor_4_out, and_4_out);
  xor xor_22 (out_21, xor_21_out, in_12);
  and and_11 (and_11_out, xor_4_out, and_4_out);
  or or_5 (or_5_out, and_11_out, and_12_out);
  and and_12 (and_12_out, xor_4_out, in_12);
  and and_13 (and_13_out, and_4_out, in_12);
  or or_6 (or_6_out, or_5_out, and_13_out);
  xor xor_23 (xor_23_out, xor_3_out, and_3_out);
  and and_14 (and_14_out, xor_3_out, and_3_out);
  and and_15 (and_15_out, xor_3_out, or_6_out);
  and and_16 (and_16_out, and_3_out, or_6_out);
  xor xor_24 (out_22, xor_23_out, or_6_out);
  or or_7 (or_7_out, and_14_out, and_15_out);
  or or_8 (or_8_out, or_7_out, and_16_out);
  xor xor_25 (xor_25_out, xor_2_out, and_2_out);
  xor xor_26 (out_23, xor_25_out, or_8_out);
  and and_17 (and_17_out, xor_2_out, and_2_out);
  or or_9 (or_9_out, and_17_out, and_18_out);
  and and_18 (and_18_out, xor_2_out, or_8_out);
  and and_19 (and_19_out, and_2_out, or_8_out);
  or or_10 (or_10_out, or_9_out, and_19_out);
  xor xor_27 (xor_27_out, undriven_5, undriven_6);
  and and_20 (and_20_out, undriven_5, undriven_6);
  and and_21 (and_21_out, undriven_5, undriven_7);
  and and_22 (and_22_out, undriven_6, undriven_7);
  xor xor_28 (xor_28_out, xor_1_out, and_1_out);
  and and_23 (and_23_out, xor_1_out, and_1_out);
  and and_24 (and_24_out, xor_1_out, or_10_out);
  and and_25 (and_25_out, and_1_out, or_10_out);
  xor xor_29 (xor_29_out, xor_27_out, undriven_7);
  or or_11 (or_11_out, and_20_out, and_21_out);
  or or_12 (or_12_out, or_11_out, and_22_out);
  xor xor_30 (out_24, xor_28_out, or_10_out);
  or or_13 (or_13_out, and_23_out, and_24_out);
  or or_14 (or_14_out, or_13_out, and_25_out);
endmodule
